# Fritzing sketch fan-speed-controller (saved by Fritzing 0.9.9b)
circuit board: 4cm x 4.5cm
stripboards: 1

parts:
  7805 = Voltage Regulator [package=to220-igo]
  10kΩ = Resistor [tolerance=±5% resistance=10k power=0.25 package=THT]
  Terminal_Block = Camdenboss CTB0158-7 [part_number=CTB0158-7 package=THT]
  1kΩ = Resistor [tolerance=±5% resistance=1k power=0.25 package=THT]
  100nf = Ceramic Capacitor [capacitance=100nF voltage=35V package="100 mil [THT, multilayer]"]
  330nf = Ceramic Capacitor [capacitance=0pF voltage=35V package="100 mil [THT, multilayer]"]
  20kΩ = Resistor [tolerance=±5% resistance=22k power=0.25 package=THT]
  ATTINY85 = attiny85 [package=dip]
  STA509A_MOSFET_Array = mystery part, 10 pins [chip_label=?]
  PC817 = Sharp PC817 [package=THT]
  IFR4095 = Basic FET P-Channel [part_number=IFR4092 package="TO220 [THT]"]
  2_2Ω = Resistor [tolerance=±5% resistance=1k power=0.25 package=THT]
  20kΩ_2 = Resistor [tolerance=±5% resistance=22k power=0.25 package=THT]

nets:
  N1: 7805.GND, Terminal_Block.pin6, 100nf.1, 330nf.0, 20kΩ.Pin_1, ATTINY85.Pin_4, STA509A_MOSFET_Array.pin1, STA509A_MOSFET_Array.pin10, PC817.Pin_2, PC817.Pin_3, 20kΩ_2.Pin_1
  N2: 7805.IN, Terminal_Block.pin1, 1kΩ.Pin_0, 330nf.1, IFR4095.source
  N3: 7805.OUT, 10kΩ.Pin_1, 100nf.0, ATTINY85.Pin_8
  N4: 10kΩ.Pin_0, ATTINY85.Pin_1
  N5: Terminal_Block.pin2, STA509A_MOSFET_Array.pin2
  N6: Terminal_Block.pin3, STA509A_MOSFET_Array.pin4
  N7: Terminal_Block.pin4, STA509A_MOSFET_Array.pin6
  N8: Terminal_Block.pin5, STA509A_MOSFET_Array.pin8
  N9: Terminal_Block.pin7, 2_2Ω.Pin_0
  N10: 1kΩ.Pin_1, PC817.Pin_4, IFR4095.gate
  N11: 20kΩ.Pin_0, ATTINY85.Pin_3, PC817.Pin_1
  N12: ATTINY85.Pin_2, STA509A_MOSFET_Array.pin9
  N13: ATTINY85.Pin_5, STA509A_MOSFET_Array.pin7
  N14: ATTINY85.Pin_6, STA509A_MOSFET_Array.pin5
  N15: ATTINY85.Pin_7, STA509A_MOSFET_Array.pin3
  N16: IFR4095.drain, 2_2Ω.Pin_1, 20kΩ_2.Pin_0

notes:
  12V
  GND
  OUT
  SW1
  SW2
  SW3
  SW4
  Fan Speed Controller v8.0
  ©2022 That Ain't Working
